# Fritzing sketch Schaltplan (saved by Fritzing 0.9.3b)
breadboards: 1

parts:
  NEOPIXEL1 = Neopixel Strip -- Black (30/m)
  Arduino_Mega = Arduino Mega 2560 (Rev3)
  NEOPIXEL2 = Neopixel Strip -- Black (30/m)
  NEOPIXEL3 = Neopixel Strip -- Black (30/m)
  NEOPIXEL4 = Neopixel Strip -- Black (30/m)
  NEOPIXEL5 = Neopixel Strip -- Black (30/m)
  NEOPIXEL6 = Neopixel Strip -- Black (30/m)
  NEOPIXEL7 = Neopixel Strip -- Black (30/m)
  NEOPIXEL8 = Neopixel Strip -- Black (30/m)
  NEOPIXEL9 = Neopixel Strip -- Black (30/m)
  NEOPIXEL10 = Neopixel Strip -- Black (30/m)
  NEOPIXEL11 = Neopixel Strip -- Black (30/m)
  NEOPIXEL12 = Neopixel Strip -- Black (30/m)
  NEOPIXEL13 = Neopixel Strip -- Black (30/m)
  NEOPIXEL14 = Neopixel Strip -- Black (30/m)
  NEOPIXEL15 = Neopixel Strip -- Black (30/m)
  NEOPIXEL16 = Neopixel Strip -- Black (30/m)
  BUTTON2 = Arcade Button (red)
  BUTTON3 = Arcade Button (red)
  BUTTON4 = Arcade Button (red)
  R1 = Resistor [tolerance=±20% resistance=1k package=THT]
  R2 = Resistor [tolerance=±20% resistance=1k package=THT]
  R3 = Resistor [tolerance=±20% resistance=1k package=THT]
  R4 = Resistor [tolerance=±20% resistance=1k package=THT]
  BUTTON1 = Arcade Button (white)
  BUTTON1_2 = Arcade Button (yellow)

nets:
  GND: NEOPIXEL1.GND#1, Arduino_Mega.GND, NEOPIXEL2.GND#1, NEOPIXEL3.GND#1, NEOPIXEL4.GND#1, R1.Pin_1, R2.Pin_1, R3.Pin_1, R4.Pin_1
  N1: NEOPIXEL1.Din, Arduino_Mega.D7_PWM
  5V: NEOPIXEL1.+5V#3, Arduino_Mega.VIN, NEOPIXEL2.+5V#3, NEOPIXEL3.+5V#3, NEOPIXEL4.+5V#3
  N2: NEOPIXEL1.+5V#4, NEOPIXEL5.+5V#3
  N3: NEOPIXEL1.Dout, NEOPIXEL5.Din
  N4: NEOPIXEL1.GND#6, NEOPIXEL5.GND#1
  N5: Arduino_Mega.D11_PWM, BUTTON4.no_name_yet#2, R1.Pin_0
  N6: Arduino_Mega.D10_PWM, BUTTON3.no_name_yet#2, R2.Pin_0
  N7: Arduino_Mega.D9_PWM, R3.Pin_0, BUTTON1.no_name_yet#2, BUTTON1_2.no_name_yet#2
  N8: Arduino_Mega.D8_PWM, BUTTON2.no_name_yet#2, R4.Pin_0
  N9: Arduino_Mega.5V, BUTTON2.no_name_yet#1, BUTTON3.no_name_yet#1, BUTTON4.no_name_yet#1, BUTTON1.no_name_yet#1, BUTTON1_2.no_name_yet#1
  N10: Arduino_Mega.D4_PWM, NEOPIXEL4.Din
  N11: Arduino_Mega.D5_PWM, NEOPIXEL3.Din
  N12: Arduino_Mega.D6_PWM, NEOPIXEL2.Din
  N13: NEOPIXEL2.+5V#4, NEOPIXEL6.+5V#3
  N14: NEOPIXEL2.Dout, NEOPIXEL6.Din
  N15: NEOPIXEL2.GND#6, NEOPIXEL6.GND#1
  N16: NEOPIXEL3.+5V#4, NEOPIXEL9.+5V#3
  N17: NEOPIXEL3.Dout, NEOPIXEL9.Din
  N18: NEOPIXEL3.GND#6, NEOPIXEL9.GND#1
  N19: NEOPIXEL4.+5V#4, NEOPIXEL11.+5V#3
  N20: NEOPIXEL4.Dout, NEOPIXEL11.Din
  N21: NEOPIXEL4.GND#6, NEOPIXEL11.GND#1
  N22: NEOPIXEL5.+5V#4, NEOPIXEL8.+5V#3
  N23: NEOPIXEL5.Dout, NEOPIXEL8.Din
  N24: NEOPIXEL5.GND#6, NEOPIXEL8.GND#1
  N25: NEOPIXEL6.+5V#4, NEOPIXEL7.+5V#3
  N26: NEOPIXEL6.Dout, NEOPIXEL7.Din
  N27: NEOPIXEL6.GND#6, NEOPIXEL7.GND#1
  N28: NEOPIXEL7.+5V#4, NEOPIXEL14.+5V
  N29: NEOPIXEL7.Dout, NEOPIXEL14.Din
  N30: NEOPIXEL7.GND#6, NEOPIXEL14.GND
  N31: NEOPIXEL8.+5V#4, NEOPIXEL13.+5V
  N32: NEOPIXEL8.Dout, NEOPIXEL13.Din
  N33: NEOPIXEL8.GND#6, NEOPIXEL13.GND
  N34: NEOPIXEL9.+5V#4, NEOPIXEL10.+5V#3
  N35: NEOPIXEL9.Dout, NEOPIXEL10.Din
  N36: NEOPIXEL9.GND#6, NEOPIXEL10.GND#1
  N37: NEOPIXEL10.+5V#4, NEOPIXEL15.+5V
  N38: NEOPIXEL10.Dout, NEOPIXEL15.Din
  N39: NEOPIXEL10.GND#6, NEOPIXEL15.GND
  N40: NEOPIXEL11.+5V#4, NEOPIXEL12.+5V#3
  N41: NEOPIXEL11.Dout, NEOPIXEL12.Din
  N42: NEOPIXEL11.GND#6, NEOPIXEL12.GND#1
  N43: NEOPIXEL12.+5V#4, NEOPIXEL16.+5V
  N44: NEOPIXEL12.Dout, NEOPIXEL16.Din
  N45: NEOPIXEL12.GND#6, NEOPIXEL16.GND

custom parts:
  Neopixel Strip -- Black (30/m): These NeoPixel strips have 30 digitally-addressable pixel LEDs per meter and are very affordable and are only 12.5 mm wide, 10 mm if you remove the strip from the casing.
  Arcade Button (red): Adafruit Arcade Button (red)
  Arcade Button (white): Adafruit Arcade Button (white)
  Arcade Button (yellow): Adafruit Arcade Button (yellow)
